// Logisim project Binary Adder.circ as structural Verilog
// HA
module Half_Adder (
  input  A,
  input  B,
  output Sum,
  output Cout
);

  xor xor_1 (Sum, A, B);
  and and_1 (Cout, A, B);
endmodule

// FA
module Full_Adder (
  input  Cin,
  input  A,
  input  B,
  output S,
  output Cout
);

  wire half_adder_1_cout, half_adder_1_sum, half_adder_2_cout;

  Half_Adder half_adder_1 (.A(A), .B(B), .Sum(half_adder_1_sum), .Cout(half_adder_1_cout));
  Half_Adder half_adder_2 (.A(Cin), .B(half_adder_1_sum), .Sum(S), .Cout(half_adder_2_cout));
  or or_1 (Cout, half_adder_2_cout, half_adder_1_cout);
endmodule

module Verrou (
  input  h,
  input  e,
  output s
);

  wire and_1_out, and_2_out, not_1_out, not_2_out, not_3_out, or_1_out;

  not not_1 (not_1_out, e);
  and and_1 (and_1_out, h, not_1_out);
  and and_2 (and_2_out, h, e);
  not not_2 (not_2_out, s);
  or or_1 (or_1_out, and_1_out, not_2_out);
  or or_2 (s, not_3_out, and_2_out);
  not not_3 (not_3_out, or_1_out);
endmodule

module Verrou_Horloge (
  input  e,
  output s
);

  wire and_1_out, and_2_out, clock_1_out, not_1_out, not_2_out, not_3_out, or_1_out;

  Clock clock_1 (.out(clock_1_out));
  not not_1 (not_1_out, e);
  and and_1 (and_1_out, clock_1_out, not_1_out);
  and and_2 (and_2_out, clock_1_out, e);
  not not_2 (not_2_out, s);
  or or_1 (or_1_out, and_1_out, not_2_out);
  or or_2 (s, not_3_out, and_2_out);
  not not_3 (not_3_out, or_1_out);
endmodule

// D
module Bascule_D (
  input  h,
  input  e,
  output s
);

  wire not_1_out, verrou_1_s;

  Verrou verrou_1 (.h(h), .e(e), .s(verrou_1_s));
  not not_1 (not_1_out, h);
  Verrou verrou_2 (.h(not_1_out), .e(verrou_1_s), .s(s));
endmodule

module Retardeur (
  input  e,
  output s
);

  wire bascule_d_1_s, bascule_d_2_s, clock_1_out;

  Clock clock_1 (.out(clock_1_out));
  Bascule_D bascule_d_1 (.h(clock_1_out), .e(e), .s(bascule_d_1_s));
  LED led_1 (.in(bascule_d_1_s));
  Bascule_D bascule_d_2 (.h(clock_1_out), .e(bascule_d_1_s), .s(bascule_d_2_s));
  LED led_2 (.in(bascule_d_2_s));
  Bascule_D bascule_d_3 (.h(clock_1_out), .e(bascule_d_2_s), .s(s));
  LED led_3 (.in(s));
endmodule

module Compteur (
  input  in_1
);

  wire bascule_d_1_s, clock_1_out, full_adder_1_s;

  Adder #(.width(1)) adder_1 ();  // open: a, b, out, cin, cout
  Full_Adder full_adder_1 (.A(bascule_d_1_s), .B(in_1), .S(full_adder_1_s));  // open: Cin, Cout
  Clock clock_1 (.out(clock_1_out));
  Bascule_D bascule_d_1 (.h(clock_1_out), .e(full_adder_1_s), .s(bascule_d_1_s));
  Hex_Digit_Display hex_digit_display_1 (.dp(bascule_d_1_s));  // open: value
endmodule

// Inc
module Incrementer (
  input  in_1,
  input  in_2,
  input  in_3,
  output out_4,
  output out_5
);

  Full_Adder full_adder_1 (.Cin(in_1), .A(in_2), .B(in_3), .S(out_4), .Cout(out_5));
endmodule
